# Fritzing sketch Práctica 3 (saved by Fritzing 0.9.3b)
breadboards: 1

parts:
  J1 = Piezo Speaker
  Componente1 = Arduino Uno (Rev3) - ICSP
  LCD1 = LCD screen
  Componente2 = Real Time Clock Module - DS1307 RTC Breakout Board
  LCM1602_IIC1 = LCM1602 IIC [part_number="LCM1602 IIC" chip_label="LCM1602 IIC" package="DIP (Dual Inline) [THT]"]
  LED1 = LED - 5mm [color="Green (570nm)" package="5 mm [THT]"]
  LED2 = LED - 5mm [color="Red (633nm)" package="5 mm [THT]"]
  LED3 = LED - 5mm [color="Yellow (595nm)" package="5 mm [THT]"]
  U1 = TEMPERATURE-SENSOR [package=to-92]
  LED5 = RGB LED - (4 legs) [package="5 mm [THT]"]
  R1 = Resistor [tolerance=±5% resistance=220 package="0805 [SMD]"]
  R2 = Resistor [tolerance=±5% resistance=220 package="0805 [SMD]"]
  R3 = Resistor [tolerance=±5% resistance=220 package="0805 [SMD]"]

nets:
  N1: J1.pin2, Componente1.D3_PWM
  N2: Componente1.A0, U1.ADJ
  N3: Componente1.A4/SDA, Componente2.SQW, LCM1602_IIC1.SDA
  N4: Componente1.A5/SCL, Componente2.SCL, LCM1602_IIC1.SCL
  N5: Componente1.D9_PWM, LED5.red_cathode
  N6: Componente1.D10_PWM/SS, LED5.green_cathode
  N7: Componente1.D11_PWM/MOSI, LED5.blue_cathode
  5V: Componente1.5V, Componente2.5V, LCM1602_IIC1.VCC, U1.VCC, R1.Pin_1, R2.Pin_1, R3.Pin_1
  GND: Componente1.GND, Componente2.GND, LCM1602_IIC1.GND, LED1.cathode, LED2.cathode, LED3.cathode, U1.GND, LED5.common_anode
  VSS: LCD1.VSS, LCM1602_IIC1.VSS
  VDD: LCD1.VDD, LCM1602_IIC1.VDD
  N8: LCD1.V0, LCM1602_IIC1.V0
  N9: LCD1.RS, LCM1602_IIC1.RS
  N10: LCD1.R/W, LCM1602_IIC1.RW
  N11: LCD1.E, LCM1602_IIC1.E
  N12: LCD1.DB0, LCM1602_IIC1.D0
  N13: LCD1.DB1, LCM1602_IIC1.D1
  N14: LCD1.DB2, LCM1602_IIC1.D2
  N15: LCD1.DB3, LCM1602_IIC1.D3
  N16: LCD1.DB4, LCM1602_IIC1.D4
  N17: LCD1.DB5, LCM1602_IIC1.D5
  N18: LCD1.DB6, LCM1602_IIC1.D6
  N19: LCD1.DB7, LCM1602_IIC1.D7
  N20: LCD1.LED+, LCM1602_IIC1.A
  N21: LCD1.LED-, LCM1602_IIC1.K
  N22: LED1.anode, R2.Pin_0
  N23: LED2.anode, R3.Pin_0
  N24: LED3.anode, R1.Pin_0

custom parts:
  LCM1602 IIC: I2C-Module to use a 1602 or 2004 LCD on with the wire.h libory Serial LCD Modul
